// Logisim project simpleGates.circ as structural Verilog: 1 circuit, main circuit main
module main (
);

  wire nand_1_out, nand_3_out, nand_5_out, undriven, undriven_2, undriven_3, undriven_4;

  nand nand_1 (nand_1_out, undriven, undriven_2);
  // NAND_Gate nand_2 has open pins: in0=nand_1_out, in1=nand_1_out, out=open
  nand nand_3 (nand_3_out, undriven_3, undriven_3);
  // NAND_Gate nand_4 has open pins: in0=nand_3_out, in1=nand_5_out, out=open
  nand nand_5 (nand_5_out, undriven_4, undriven_4);

  // Notes on the sheet:
  //   AND with NAND
  //   OR with NAND
endmodule
